# Fritzing sketch Lab1_Schematic (saved by Fritzing 0.9.9b)
breadboards: 2

parts:
  7_Segment_4_Digit_Display1 = 7-SEGMENT-4DIGIT common cathode [part_number=HS420561K-32 package=7-segment-4digit-cathode]
  Part1 = Arduino Mega 2560 (Rev3)
  U1 = 74HC595 [package="DIP16 [THT]"]
  Q1 = TRANSISTOR_NPN [package=to-92-ammo]
  Q2 = TRANSISTOR_NPN [package=to-92-ammo]
  R2 = Resistor [tolerance=±5% power=0.25 resistance=4.7k package=THT]
  R1 = Resistor [tolerance=±5% power=0.25 resistance=4.7k package=THT]
  R3 = Resistor [tolerance=±5% power=0.25 resistance=220 package=THT]
  R4 = Resistor [tolerance=±5% power=0.25 resistance=220 package=THT]
  R5 = Resistor [tolerance=±5% power=0.25 resistance=220 package=THT]
  R6 = Resistor [tolerance=±5% power=0.25 resistance=220 package=THT]
  R7 = Resistor [tolerance=±5% power=0.25 resistance=220 package=THT]
  R9 = Resistor [tolerance=±5% power=0.25 resistance=220 package=THT]
  R10 = Resistor [tolerance=±5% power=0.25 resistance=220 package=THT]
  R8 = Resistor [tolerance=±5% power=0.25 resistance=220 package=THT]
  S1 = Pushbutton [package="[SMD]"]
  R11 = Resistor [tolerance=±5% power=0.25 resistance=10000 package=THT]
  LED1 = smd LED [color="Red (633nm)" package="1206 [SMD]"]
  LED2 = LED - 5mm [color="Green (555nm)" current=0.030 package="5 mm [THT]"]
  LED3 = LED - 5mm [color="Yellow (595nm)" current=0.030 package="5 mm [THT]"]
  R12 = Resistor [tolerance=±5% power=0.25 resistance=220 package=THT]
  R13 = Resistor [tolerance=±5% power=0.25 resistance=220 package=THT]
  R14 = Resistor [tolerance=±5% power=0.25 resistance=220 package=THT]
  J1 = Piezo Speaker
  R15 = Resistor [tolerance=±5% power=0.25 resistance=100 package=THT]

nets:
  N1: 7_Segment_4_Digit_Display1.pin_1, R8.Pin_0
  N2: 7_Segment_4_Digit_Display1.pin_2, R9.Pin_0
  N3: 7_Segment_4_Digit_Display1.pin_3, R3.Pin_0
  N4: 7_Segment_4_Digit_Display1.pin_4, R4.Pin_0
  N5: 7_Segment_4_Digit_Display1.pin_5, R5.Pin_0
  N6: 7_Segment_4_Digit_Display1.pin_7, R10.Pin_0
  N7: 7_Segment_4_Digit_Display1.pin_8, Q1.E
  N8: 7_Segment_4_Digit_Display1.pin_9, Q2.E
  N9: 7_Segment_4_Digit_Display1.pin_10, R7.Pin_0
  N10: 7_Segment_4_Digit_Display1.pin_11, R6.Pin_0
  N11: Part1.D11_PWM, R15.Pin_1
  N12: Part1.D10_PWM, LED3.cathode
  N13: Part1.D9_PWM, LED2.cathode
  N14: Part1.D8_PWM, LED1.cathode
  5V: Part1.5V, U1.MR, U1.VCC
  GND: Part1.GND, U1.GND, U1.OE, Q1.C, Q2.C, S1.Pin_3, S1.Pin_4, R11.Pin_1, R12.Pin_1, R13.Pin_1, R14.Pin_1, J1.pin1
  N15: Part1.D2_PWM, R1.Pin_0
  N16: Part1.D3_PWM, R2.Pin_0
  N17: Part1.D4_PWM, U1.DS
  N18: Part1.D5_PWM, U1.ST_CP
  N19: Part1.D6_PWM, U1.SH_CP
  N20: U1.Q1, R7.Pin_1
  N21: U1.Q2, R10.Pin_1
  N22: U1.Q3, R8.Pin_1
  N23: U1.Q4, R9.Pin_1
  N24: U1.Q5, R3.Pin_1
  N25: U1.Q6, R4.Pin_1
  N26: U1.Q7, R5.Pin_1
  N27: U1.Q0, R6.Pin_1
  N28: Q1.B, R1.Pin_1
  N29: Q2.B, R2.Pin_1
  N30: S1.Pin_1, S1.Pin_2, R11.Pin_0
  N31: LED1.anode, R12.Pin_0
  N32: LED2.anode, R13.Pin_0
  N33: LED3.anode, R14.Pin_0
  N34: J1.pin2, R15.Pin_0

custom parts:
  7-SEGMENT-4DIGIT common cathode: A 7 Segment 4 Digit common cathode display, with decimal points
