# Fritzing sketch Lab2_Schematic (saved by Fritzing 0.9.9b)
breadboards: 1

parts:
  Part1 = Arduino Mega 2560 (Rev3)
  S1 = Pushbutton [package="[SMD]"]
  R11 = Resistor [tolerance=±5% power=0.25 resistance=10000 package=THT]
  J1 = Piezo Speaker
  R15 = Resistor [tolerance=±5% power=0.25 resistance=100 package=THT]
  Part2 = InvenSense MPU6050
  Part3 = Thumb Joystick

nets:
  N1: Part1.A0, Part3.HORZ
  N2: Part1.A1, Part3.VERT
  N3: Part1.SCL, Part2.SCL
  N4: Part1.SDA, Part2.SDA
  GND: Part1.GND, R11.Pin_1, J1.pin1, Part2.GND, Part3.GND
  3V3: Part1.3V3, Part2.VCC
  5V: Part1.5V, S1.Pin_3, S1.Pin_4, Part3.VCC
  N5: Part1.D2_PWM, Part3.SEL
  N6: Part1.D3_PWM, S1.Pin_1, S1.Pin_2, R11.Pin_0
  N7: Part1.D4_PWM, R15.Pin_1
  N8: J1.pin2, R15.Pin_0
