# Fritzing sketch Lab3_Schematic (saved by Fritzing 0.9.9b)
breadboards: 2

parts:
  Part1 = Arduino Mega 2560 (Rev3)
  S1 = Pushbutton [package="[SMD]"]
  R11 = Resistor [tolerance=±5% power=0.25 resistance=10000 package=THT]
  IC1 = L293D [package=THT]
  M1 = DC Motor
  Part3 = Real Time Clock Module - DS1307 RTC Breakout Board
  U1 = LCD-16X2 [package=lcd-16x2_noholes]  # not connected
  R12 = Trimmer Potentiometer [maximum_resistance=10kΩ package=THT]
  Mod1 = KY-022 Infrared Receiver Module [package="Breakout board"]
  YwRobot_Power_Supply1 = YwRobot Breadboard Power Supply [part_number=545043]

nets:
  N1: Part1.D21/SCL, Part3.SCL
  N2: Part1.D20/SDA, Part3.SDA
  5V: Part1.5V, Part3.5V, R12.leg1, Mod1.Vin
  GND: Part1.GND, S1.Pin_3, S1.Pin_4, R11.Pin_1, Part3.GND, R12.leg2, Mod1.-
  N3: Part1.D2_PWM, Mod1.S
  N4: Part1.D3_PWM, IC1.In_2
  N5: Part1.D4_PWM, IC1.In_1
  N6: Part1.D5_PWM, IC1.Enable_1
  N7: Part1.D6_PWM, S1.Pin_1, S1.Pin_2, R11.Pin_0
  N8: IC1.Out_1_(_Controlled_by_Enable_1_), M1.pin_1
  N9: IC1.0V, YwRobot_Power_Supply1.GND
  N10: IC1.Out_2_(_Controlled_by_Enable_1_), M1.pin_2
  N11: IC1.+Vmotor, YwRobot_Power_Supply1.VCC

custom parts:
  KY-022 Infrared Receiver Module: KY-022 IR receiver module, reacts to 38kHz infrared light.
  YwRobot Breadboard Power Supply: The YwRobot Breadboard Power Supply (MB-V2) has two power rails; they can be 5V or 3V3. Power to the module can be provided through the female USB socket or through the A10 (female) 2.1mm power jack.
